# Fritzing sketch BounceTest (saved by Fritzing 0.7.12b)
breadboards: 1

parts:
  Arduino1 = Arduino
  R1 = Resistor [tolerance=±5% resistance=220 package=THT]
  S1 = Pushbutton [package=THT]

nets:
  N1: Arduino1.D13, R1.Pin_1, S1.leg1
  N2: Arduino1.3V3, S1.leg0
  N3: Arduino1.GND, R1.Pin_0
