# Fritzing sketch TempSensor (saved by Fritzing 0.7.12b)
breadboards: 1

parts:
  LED1 = LED - 5mm [color="Red (633nm)" package="5 mm [THT]"]
  LED2 = LED - 5mm [color="Orange (620nm)" package="5 mm [THT]"]
  LED3 = LED - 5mm [color="Green (565nm)" package="5 mm [THT]"]
  R1 = Resistor [tolerance=±5% resistance=220 package=THT]
  R2 = Resistor [tolerance=±5% resistance=220 package=THT]
  R3 = Resistor [tolerance=±5% resistance=220 package=THT]
  R4 = Resistor [tolerance=±5% resistance=4.0k package=THT]
  R5 = Temperature Sensor (Thermistor) [package=THT]
  Arduino1 = Arduino

nets:
  N1: LED1.cathode, LED2.cathode, LED3.cathode, R4.Pin_0, Arduino1.GND
  N2: LED1.anode, R1.Pin_1
  N3: LED2.anode, R2.Pin_1
  N4: LED3.anode, R3.Pin_1
  N5: R1.Pin_0, Arduino1.D11
  N6: R2.Pin_0, Arduino1.D12
  N7: R3.Pin_0, Arduino1.D13
  N8: R4.Pin_1, R5.pin_0, Arduino1.A0
  N9: R5.pin_1, Arduino1.+5V
