# Fritzing sketch TrafficLights2 (saved by Fritzing 0.7.12b)
breadboards: 1

parts:
  LED1 = LED - 5mm [color="Red (633nm)" package="5 mm [THT]"]
  LED2 = LED - 5mm [color="Orange (620nm)" package="5 mm [THT]"]
  LED3 = LED - 5mm [color="Green (565nm)" package="5 mm [THT]"]
  LED4 = LED - 5mm [color="Red (633nm)" package="5 mm [THT]"]
  LED5 = LED - 5mm [color="Orange (620nm)" package="5 mm [THT]"]
  LED6 = LED - 5mm [color="Green (565nm)" package="5 mm [THT]"]
  R1 = Resistor [tolerance=±5% resistance=220 package=THT]
  R2 = Resistor [tolerance=±5% resistance=220 package=THT]
  R3 = Resistor [tolerance=±5% resistance=220 package=THT]
  R4 = Resistor [tolerance=±5% resistance=220 package=THT]
  R5 = Resistor [tolerance=±5% resistance=220 package=THT]
  R6 = Resistor [tolerance=±5% resistance=220 package=THT]
  R7 = Resistor [tolerance=±5% resistance=220 package=THT]
  Arduino1 = Arduino
  S2 = Pushbutton [package=THT]

nets:
  N1: LED1.cathode, LED2.cathode, LED3.cathode, LED4.cathode, LED5.cathode, LED6.cathode, R7.Pin_1, Arduino1.GND
  N2: LED1.anode, R1.Pin_0
  N3: LED2.anode, R6.Pin_0
  N4: LED3.anode, R5.Pin_0
  N5: LED4.anode, R3.Pin_0
  N6: LED5.anode, R2.Pin_0
  N7: LED6.anode, R4.Pin_0
  N8: R1.Pin_1, Arduino1.D13
  N9: R2.Pin_1, Arduino1.D9
  N10: R3.Pin_1, Arduino1.D10
  N11: R4.Pin_1, Arduino1.D8
  N12: R5.Pin_1, Arduino1.D11
  N13: R6.Pin_1, Arduino1.D12
  N14: R7.Pin_0, Arduino1.D7, S2.leg0
  N15: Arduino1.+5V, S2.leg1
